// Logisim project Booths_28_bitsss.circ as structural Verilog: 11 circuits, main circuit Booth's multiplier
module Booth_s_multiplier (
  input  [27:0] MBRout,
  input  [27:0] Ac,
  input  bStart,
  input  in_4,
  output [27:0] BoothsH,
  output [27:0] BoothsL,
  output busy
);

  wire A_out, controller_1_c0, controller_1_c1, controller_1_cl__a__q_1, controller_1_dec_cnt,
       controller_1_load__m__q__cnt, controller_1_load_a, controller_1_shr, nor_1_out, or_1_out, Q_1_q0,
       Q_out;
  wire [4:0] counter_1_q;
  wire [27:0] M_q27, n28bit_alu_1_result;

  Controller controller_1 (
    .Clk(in_4), .Q0(BoothsL[0]), .Q_1(Q_1_q0), .Count(counter_1_q), .C0(controller_1_c0),
    .C1(controller_1_c1), .Shr(controller_1_shr), .Dec_Cnt(controller_1_dec_cnt),
    .Cl__A__Q_1(controller_1_cl__a__q_1), .Load_A(controller_1_load_a),
    .LOad__M__Q__Cnt(controller_1_load__m__q__cnt), .Reset(bStart));
  or or_1 (or_1_out, controller_1_load__m__q__cnt, controller_1_dec_cnt);
  Counter #(.width(5), .max('h1f)) counter_1 (
    .load(or_1_out), .D(5'b11100), .count(controller_1_dec_cnt), .Q(counter_1_q), .clk(in_4));  // open: carry, clr
  nor nor_1 (nor_1_out, counter_1_q[4], counter_1_q[3], counter_1_q[2], counter_1_q[1], counter_1_q[0]);
  not not_1 (busy, nor_1_out);
  Shift_Register #(.length(28)) M (
    .shift(1'b0), .clk(in_4), .load(controller_1_load__m__q__cnt), .d0(MBRout[27]), .q0(M_q27[27]),
    .d1(MBRout[26]), .q1(M_q27[26]), .d2(MBRout[25]), .q2(M_q27[25]), .d3(MBRout[24]), .q3(M_q27[24]),
    .d4(MBRout[23]), .q4(M_q27[23]), .d5(MBRout[22]), .q5(M_q27[22]), .d6(MBRout[21]), .q6(M_q27[21]),
    .d7(MBRout[20]), .q7(M_q27[20]), .d8(MBRout[19]), .q8(M_q27[19]), .d9(MBRout[18]), .q9(M_q27[18]),
    .d10(MBRout[17]), .q10(M_q27[17]), .d11(MBRout[16]), .q11(M_q27[16]), .d12(MBRout[15]), .q12(M_q27[15]),
    .d13(MBRout[14]), .q13(M_q27[14]), .d14(MBRout[13]), .q14(M_q27[13]), .d15(MBRout[12]), .q15(M_q27[12]),
    .d16(MBRout[11]), .q16(M_q27[11]), .d17(MBRout[10]), .q17(M_q27[10]), .d18(MBRout[9]), .q18(M_q27[9]),
    .d19(MBRout[8]), .q19(M_q27[8]), .d20(MBRout[7]), .q20(M_q27[7]), .d21(MBRout[6]), .q21(M_q27[6]),
    .d22(MBRout[5]), .q22(M_q27[5]), .d23(MBRout[4]), .q23(M_q27[4]), .d24(MBRout[3]), .q24(M_q27[3]),
    .d25(MBRout[2]), .q25(M_q27[2]), .d26(MBRout[1]), .q26(M_q27[1]), .d27(MBRout[0]), .q27(M_q27[0]));  // open: in, out, clr
  Shift_Register #(.length(28)) A (
    .shift(controller_1_shr), .in(BoothsH[27]), .clk(in_4), .out(A_out), .load(controller_1_load_a),
    .clr(controller_1_cl__a__q_1), .d0(n28bit_alu_1_result[27]), .q0(BoothsH[27]),
    .d1(n28bit_alu_1_result[26]), .q1(BoothsH[26]), .d2(n28bit_alu_1_result[25]), .q2(BoothsH[25]),
    .d3(n28bit_alu_1_result[24]), .q3(BoothsH[24]), .d4(n28bit_alu_1_result[23]), .q4(BoothsH[23]),
    .d5(n28bit_alu_1_result[22]), .q5(BoothsH[22]), .d6(n28bit_alu_1_result[21]), .q6(BoothsH[21]),
    .d7(n28bit_alu_1_result[20]), .q7(BoothsH[20]), .d8(n28bit_alu_1_result[19]), .q8(BoothsH[19]),
    .d9(n28bit_alu_1_result[18]), .q9(BoothsH[18]), .d10(n28bit_alu_1_result[17]), .q10(BoothsH[17]),
    .d11(n28bit_alu_1_result[16]), .q11(BoothsH[16]), .d12(n28bit_alu_1_result[15]), .q12(BoothsH[15]),
    .d13(n28bit_alu_1_result[14]), .q13(BoothsH[14]), .d14(n28bit_alu_1_result[13]), .q14(BoothsH[13]),
    .d15(n28bit_alu_1_result[12]), .q15(BoothsH[12]), .d16(n28bit_alu_1_result[11]), .q16(BoothsH[11]),
    .d17(n28bit_alu_1_result[10]), .q17(BoothsH[10]), .d18(n28bit_alu_1_result[9]), .q18(BoothsH[9]),
    .d19(n28bit_alu_1_result[8]), .q19(BoothsH[8]), .d20(n28bit_alu_1_result[7]), .q20(BoothsH[7]),
    .d21(n28bit_alu_1_result[6]), .q21(BoothsH[6]), .d22(n28bit_alu_1_result[5]), .q22(BoothsH[5]),
    .d23(n28bit_alu_1_result[4]), .q23(BoothsH[4]), .d24(n28bit_alu_1_result[3]), .q24(BoothsH[3]),
    .d25(n28bit_alu_1_result[2]), .q25(BoothsH[2]), .d26(n28bit_alu_1_result[1]), .q26(BoothsH[1]),
    .d27(n28bit_alu_1_result[0]), .q27(BoothsH[0]));
  _28bit_ALU u_28bit_alu_1 (
    .A(BoothsH), .B(M_q27), .Result(n28bit_alu_1_result), .Control0(controller_1_c0),
    .Control1(controller_1_c1));  // open: Zero, Negative, Overflow, Carry
  Shift_Register #(.length(28)) Q (
    .shift(controller_1_shr), .in(A_out), .clk(in_4), .out(Q_out), .load(controller_1_load__m__q__cnt),
    .d0(Ac[27]), .q0(BoothsL[27]), .d1(Ac[26]), .q1(BoothsL[26]), .d2(Ac[25]), .q2(BoothsL[25]), .d3(Ac[24]),
    .q3(BoothsL[24]), .d4(Ac[23]), .q4(BoothsL[23]), .d5(Ac[22]), .q5(BoothsL[22]), .d6(Ac[21]),
    .q6(BoothsL[21]), .d7(Ac[20]), .q7(BoothsL[20]), .d8(Ac[19]), .q8(BoothsL[19]), .d9(Ac[18]),
    .q9(BoothsL[18]), .d10(Ac[17]), .q10(BoothsL[17]), .d11(Ac[16]), .q11(BoothsL[16]), .d12(Ac[15]),
    .q12(BoothsL[15]), .d13(Ac[14]), .q13(BoothsL[14]), .d14(Ac[13]), .q14(BoothsL[13]), .d15(Ac[12]),
    .q15(BoothsL[12]), .d16(Ac[11]), .q16(BoothsL[11]), .d17(Ac[10]), .q17(BoothsL[10]), .d18(Ac[9]),
    .q18(BoothsL[9]), .d19(Ac[8]), .q19(BoothsL[8]), .d20(Ac[7]), .q20(BoothsL[7]), .d21(Ac[6]),
    .q21(BoothsL[6]), .d22(Ac[5]), .q22(BoothsL[5]), .d23(Ac[4]), .q23(BoothsL[4]), .d24(Ac[3]),
    .q24(BoothsL[3]), .d25(Ac[2]), .q25(BoothsL[2]), .d26(Ac[1]), .q26(BoothsL[1]), .d27(Ac[0]),
    .q27(BoothsL[0]));  // open: clr
  Shift_Register #(.length(1)) Q_1 (
    .shift(controller_1_shr), .in(Q_out), .clk(in_4), .clr(controller_1_cl__a__q_1), .q0(Q_1_q0));  // open: out, load, d0
endmodule

// 28-bit AND
module _28_bit_and (
  input  [27:0] A,
  input  [27:0] B,
  output [27:0] Result
);

  assign Result = A & B;  // AND_Gate and_1, 28 bits wide
endmodule

// 28-bit OR
module _28_bit_OR (
  input  [27:0] A,
  input  [27:0] B,
  output [27:0] Result
);

  assign Result = A | B;  // OR_Gate or_1, 28 bits wide
endmodule

module Full_adder (
  input  Carry_in,
  input  A,
  input  B,
  output Result,
  output Carry_out
);

  wire and_1_out, and_2_out, xor_1_out;

  and and_1 (and_1_out, B, A);
  xor xor_1 (xor_1_out, A, B);
  or or_1 (Carry_out, and_1_out, and_2_out);
  and and_2 (and_2_out, xor_1_out, Carry_in);
  xor xor_2 (Result, Carry_in, xor_1_out);
endmodule

module _28_bit_full_adder (
  input  Cin,
  input  [27:0] A,
  input  [27:0] B,
  output [27:0] \output ,
  output Cout
);

  wire full_adder_1_carry_out, full_adder_2_carry_out, full_adder_3_carry_out, full_adder_4_carry_out,
       full_adder_5_carry_out, full_adder_6_carry_out, full_adder_7_carry_out, full_adder_8_carry_out,
       full_adder_9_carry_out, full_adder_10_carry_out, full_adder_11_carry_out, full_adder_12_carry_out,
       full_adder_13_carry_out, full_adder_14_carry_out, full_adder_15_carry_out, full_adder_16_carry_out,
       full_adder_17_carry_out, full_adder_18_carry_out, full_adder_19_carry_out, full_adder_20_carry_out,
       full_adder_21_carry_out, full_adder_22_carry_out, full_adder_23_carry_out, full_adder_24_carry_out,
       full_adder_25_carry_out, full_adder_26_carry_out, full_adder_27_carry_out;

  Full_adder full_adder_1 (
    .Carry_in(Cin), .A(A[0]), .B(B[0]), .Result(\output [0]), .Carry_out(full_adder_1_carry_out));
  Full_adder full_adder_2 (
    .Carry_in(full_adder_1_carry_out), .A(A[1]), .B(B[1]), .Result(\output [1]),
    .Carry_out(full_adder_2_carry_out));
  Full_adder full_adder_3 (
    .Carry_in(full_adder_2_carry_out), .A(A[2]), .B(B[2]), .Result(\output [2]),
    .Carry_out(full_adder_3_carry_out));
  Full_adder full_adder_4 (
    .Carry_in(full_adder_3_carry_out), .A(A[3]), .B(B[3]), .Result(\output [3]),
    .Carry_out(full_adder_4_carry_out));
  Full_adder full_adder_5 (
    .Carry_in(full_adder_4_carry_out), .A(A[4]), .B(B[4]), .Result(\output [4]),
    .Carry_out(full_adder_5_carry_out));
  Full_adder full_adder_6 (
    .Carry_in(full_adder_5_carry_out), .A(A[5]), .B(B[5]), .Result(\output [5]),
    .Carry_out(full_adder_6_carry_out));
  Full_adder full_adder_7 (
    .Carry_in(full_adder_6_carry_out), .A(A[6]), .B(B[6]), .Result(\output [6]),
    .Carry_out(full_adder_7_carry_out));
  Full_adder full_adder_8 (
    .Carry_in(full_adder_7_carry_out), .A(A[7]), .B(B[7]), .Result(\output [7]),
    .Carry_out(full_adder_8_carry_out));
  Full_adder full_adder_9 (
    .Carry_in(full_adder_8_carry_out), .A(A[8]), .B(B[8]), .Result(\output [8]),
    .Carry_out(full_adder_9_carry_out));
  Full_adder full_adder_10 (
    .Carry_in(full_adder_9_carry_out), .A(A[9]), .B(B[9]), .Result(\output [9]),
    .Carry_out(full_adder_10_carry_out));
  Full_adder full_adder_11 (
    .Carry_in(full_adder_10_carry_out), .A(A[10]), .B(B[10]), .Result(\output [10]),
    .Carry_out(full_adder_11_carry_out));
  Full_adder full_adder_12 (
    .Carry_in(full_adder_11_carry_out), .A(A[11]), .B(B[11]), .Result(\output [11]),
    .Carry_out(full_adder_12_carry_out));
  Full_adder full_adder_13 (
    .Carry_in(full_adder_12_carry_out), .A(A[12]), .B(B[12]), .Result(\output [12]),
    .Carry_out(full_adder_13_carry_out));
  Full_adder full_adder_14 (
    .Carry_in(full_adder_13_carry_out), .A(A[13]), .B(B[13]), .Result(\output [13]),
    .Carry_out(full_adder_14_carry_out));
  Full_adder full_adder_15 (
    .Carry_in(full_adder_14_carry_out), .A(A[14]), .B(B[14]), .Result(\output [14]),
    .Carry_out(full_adder_15_carry_out));
  Full_adder full_adder_16 (
    .Carry_in(full_adder_15_carry_out), .A(A[15]), .B(B[15]), .Result(\output [15]),
    .Carry_out(full_adder_16_carry_out));
  Full_adder full_adder_17 (
    .Carry_in(full_adder_16_carry_out), .A(A[16]), .B(B[16]), .Result(\output [16]),
    .Carry_out(full_adder_17_carry_out));
  Full_adder full_adder_18 (
    .Carry_in(full_adder_17_carry_out), .A(A[17]), .B(B[17]), .Result(\output [17]),
    .Carry_out(full_adder_18_carry_out));
  Full_adder full_adder_19 (
    .Carry_in(full_adder_18_carry_out), .A(A[18]), .B(B[18]), .Result(\output [18]),
    .Carry_out(full_adder_19_carry_out));
  Full_adder full_adder_20 (
    .Carry_in(full_adder_19_carry_out), .A(A[19]), .B(B[19]), .Result(\output [19]),
    .Carry_out(full_adder_20_carry_out));
  Full_adder full_adder_21 (
    .Carry_in(full_adder_20_carry_out), .A(A[20]), .B(B[20]), .Result(\output [20]),
    .Carry_out(full_adder_21_carry_out));
  Full_adder full_adder_22 (
    .Carry_in(full_adder_21_carry_out), .A(A[21]), .B(B[21]), .Result(\output [21]),
    .Carry_out(full_adder_22_carry_out));
  Full_adder full_adder_23 (
    .Carry_in(full_adder_22_carry_out), .A(A[22]), .B(B[22]), .Result(\output [22]),
    .Carry_out(full_adder_23_carry_out));
  Full_adder full_adder_24 (
    .Carry_in(full_adder_23_carry_out), .A(A[23]), .B(B[23]), .Result(\output [23]),
    .Carry_out(full_adder_24_carry_out));
  Full_adder full_adder_25 (
    .Carry_in(full_adder_24_carry_out), .A(A[24]), .B(B[24]), .Result(\output [24]),
    .Carry_out(full_adder_25_carry_out));
  Full_adder full_adder_26 (
    .Carry_in(full_adder_25_carry_out), .A(A[25]), .B(B[25]), .Result(\output [25]),
    .Carry_out(full_adder_26_carry_out));
  Full_adder full_adder_27 (
    .Carry_in(full_adder_26_carry_out), .A(A[26]), .B(B[26]), .Result(\output [26]),
    .Carry_out(full_adder_27_carry_out));
  Full_adder full_adder_28 (
    .Carry_in(full_adder_27_carry_out), .A(A[27]), .B(B[27]), .Result(\output [27]), .Carry_out(Cout));
endmodule

module _28_bit_xor (
  input  Control,
  input  [27:0] B,
  output [27:0] Result
);

  wire [27:0] bit_extender_1_out;

  assign bit_extender_1_out = {{27{Control}}, Control};  // Bit_Extender bit_extender_1
  assign Result = bit_extender_1_out ^ B;  // XOR_Gate xor_1, 28 bits wide
endmodule

// 28-bit \nADD/SUB
module Add_sub (
  input  Sub,
  input  [27:0] A,
  input  [27:0] B,
  output [27:0] Result,
  output Carry,
  output Overflow
);

  wire and_1_out, and_2_out, not_1_out, not_2_out, not_3_out, sign_bit_out_1_ms_bit, sign_bit_out_2_ms_bit,
       sign_bit_out_3_ms_bit;
  wire [27:0] n28_bit_xor_1_result;

  sign_bit_out sign_bit_out_1 (.Input(A), .MS_bit(sign_bit_out_1_ms_bit));
  not not_1 (not_1_out, sign_bit_out_1_ms_bit);
  _28_bit_xor u_28_bit_xor_1 (.B(B), .Result(n28_bit_xor_1_result), .Control(Sub));
  sign_bit_out sign_bit_out_2 (.Input(n28_bit_xor_1_result), .MS_bit(sign_bit_out_2_ms_bit));
  not not_2 (not_2_out, sign_bit_out_2_ms_bit);
  _28_bit_full_adder u_28_bit_full_adder_1 (
    .A(A), .B(n28_bit_xor_1_result), .\output (Result), .Cin(Sub), .Cout(Carry));
  sign_bit_out sign_bit_out_3 (.Input(Result), .MS_bit(sign_bit_out_3_ms_bit));
  not not_3 (not_3_out, sign_bit_out_3_ms_bit);
  and and_1 (and_1_out, not_3_out, sign_bit_out_2_ms_bit, sign_bit_out_1_ms_bit);
  and and_2 (and_2_out, sign_bit_out_3_ms_bit, not_2_out, not_1_out);
  or or_1 (Overflow, and_1_out, and_2_out);
endmodule

// 27th
module sign_bit_out (
  input  [27:0] Input,
  output MS_bit
);


  assign MS_bit = Input[27];
endmodule

// Reduce-OR
module _28_bit_reduce_or (
  input  [27:0] Input,
  output \output 
);

  or or_1 (\output , Input[0], Input[1], Input[2], Input[3], Input[4], Input[5], Input[6], Input[7], Input[8], Input[9], Input[10], Input[11], Input[12], Input[13], Input[14], Input[15], Input[16], Input[17], Input[18], Input[19], Input[20], Input[21], Input[22], Input[23], Input[24], Input[25], Input[26], Input[27]);
endmodule

// 28 bit ALU
module _28bit_ALU (
  input  Control0,
  input  Control1,
  input  [27:0] A,
  input  [27:0] B,
  output [27:0] Result,
  output Zero,
  output Negative,
  output Overflow,
  output Carry
);

  wire n28_bit_reduce_or_1_output;
  wire [27:0] add_sub_1_result, multiplexer_1_out, n28_bit_and_1_result, n28_bit_or_1_result;

  _28_bit_and u_28_bit_and_1 (.A(A), .B(B), .Result(n28_bit_and_1_result));
  _28_bit_OR u_28_bit_or_1 (.A(A), .B(B), .Result(n28_bit_or_1_result));
  Add_sub add_sub_1 (.Sub(Control0), .Result(add_sub_1_result), .Carry(Carry), .Overflow(Overflow), .A(A), .B(B));
  Multiplexer #(.width(28), .enable("false")) multiplexer_1 (
    .in0(n28_bit_and_1_result), .in1(n28_bit_or_1_result), .out(multiplexer_1_out), .sel(Control0));
  Multiplexer #(.width(28), .enable("false")) multiplexer_2 (
    .in0(multiplexer_1_out), .in1(add_sub_1_result), .out(Result), .sel(Control1));
  sign_bit_out sign_bit_out_1 (.Input(Result), .MS_bit(Negative));
  _28_bit_reduce_or u_28_bit_reduce_or_1 (.Input(Result), .\output (n28_bit_reduce_or_1_output));
  not not_1 (Zero, n28_bit_reduce_or_1_output);
endmodule

// Control \nUnit
module Controller (
  input  Clk,
  input  Reset,
  input  Q0,
  input  Q_1,
  input  [4:0] Count,
  output Cl__A__Q_1,
  output LOad__M__Q__Cnt,
  output Load_A,
  output C0,
  output C1,
  output Shr,
  output Dec_Cnt
);

  wire and_3_out, multiplexer_1_out, not_1_out, not_2_out, not_3_out, not_4_out, not_5_out, not_6_out,
       not_7_out, or_2_out, Q0_prime_Q_1_out, Q0Q_1_prime_out;
  wire [1:0] rom_1_data_2;
  wire [2:0] and_1_out, and_2_out, bit_extender_1_out, bit_extender_2_out, bit_extender_3_out, CAR_q,
       or_1_out, rom_1_data;

  assign bit_extender_1_out = {{2{Q0_prime_Q_1_out}}, Q0_prime_Q_1_out};  // Bit_Extender bit_extender_1
  and Q0_prime_Q_1 (Q0_prime_Q_1_out, not_2_out, Q_1);
  not not_1 (not_1_out, Q0_prime_Q_1_out);
  assign bit_extender_2_out = {{2{not_1_out}}, not_1_out};  // Bit_Extender bit_extender_2
  assign and_1_out = 3'b100 & bit_extender_3_out & bit_extender_1_out;  // AND_Gate and_1, 3 bits wide
  assign or_1_out = and_1_out | rom_1_data | and_2_out;  // OR_Gate or_1, 3 bits wide
  not not_2 (not_2_out, Q0);
  assign and_2_out = bit_extender_2_out & bit_extender_3_out & 3'b101;  // AND_Gate and_2, 3 bits wide
  assign bit_extender_3_out = {{2{and_3_out}}, and_3_out};  // Bit_Extender bit_extender_3
  and and_3 (and_3_out, not_4_out, CAR_q[1], not_3_out);
  not not_3 (not_3_out, CAR_q[0]);
  not not_4 (not_4_out, CAR_q[2]);
  Counter #(.width(3), .max('h7)) CAR (
    .load(not_5_out), .D(or_1_out), .count(multiplexer_1_out), .Q(CAR_q), .clk(Clk), .clr(Reset));  // open: carry
  not not_5 (not_5_out, multiplexer_1_out);
  Multiplexer #(.select(2), .enable("false")) multiplexer_1 (
    .in0(1'b0), .in1(1'b1), .in2(Q0Q_1_prime_out), .in3(not_7_out), .out(multiplexer_1_out),
    .sel(rom_1_data_2));
  ROM #(.addrWidth(3), .dataWidth(12)) rom_1 (
    .addr(CAR_q), .data({Cl__A__Q_1, LOad__M__Q__Cnt, Load_A, C0, C1, Shr, Dec_Cnt, rom_1_data, rom_1_data_2}));  // open: sel
  and Q0Q_1_prime (Q0Q_1_prime_out, not_6_out, Q0);
  not not_6 (not_6_out, Q_1);
  or or_2 (or_2_out, Count[0], Count[1], Count[2], Count[3], Count[4]);
  not not_7 (not_7_out, or_2_out);

  // Notes on the sheet:
  //   To choose only
  //   state 2 (010)
  //   contents of rom_1 (hex, n*v repeats v):
  //   1 c01 2 394 281 61 b 1c
endmodule
