// Logisim project CPU_28bit.circ as structural Verilog: 3 circuits, main circuit main
module main (
  output hit,
  output miss
);

  wire clock_1_out, cpu_1_r, cpu_1_w, Reset_out;
  wire [3:0] cpu_1_addr;
  wire [27:0] cache_28bit_1_rdata, cpu_1_dataout;

  Clock clock_1 (.out(clock_1_out));
  Button Reset (.out(Reset_out));
  CPU cpu_1 (
    .Clk(clock_1_out), .Reset(Reset_out), .dataIN(cache_28bit_1_rdata), .R(cpu_1_r), .W(cpu_1_w),
    .Addr(cpu_1_addr), .DataOut(cpu_1_dataout));
  cache_28bit cache_28bit_1 (
    .clk(clock_1_out), .reset(Reset_out), .rd(cpu_1_r), .addr(cpu_1_addr), .wr(cpu_1_w),
    .Wdata(cpu_1_dataout), .Rdata(cache_28bit_1_rdata), .hit(hit), .miss(miss));

  // Notes on the sheet:
  //   0 - AND
  //   1 - ADD
  //   2 - STO
  //   3 - OR
  //   4 - SUB
  //   5 - BUN
  //   6 - LDA
  //   7 - HLT
endmodule

module CPU (
  input  [27:0] dataIN,
  input  Clk,
  input  Reset,
  output R,
  output W,
  output [3:0] Addr,
  output [27:0] DataOut
);

  wire b1, booth_s_multiplier_1_busy, bStart, c0, c1, controlunit_1_c1, controlunit_1_c2, d1, d2, LdA,
       LdA_from_MBR, LdAfrH, LdAfrL, LoadAc, LoadB, LoadMAR;
  wire [1:0] or_1_out;
  wire [3:0] counter_1_q, multiplexer_1_out;
  wire [27:0] Ac, AcIn, ALUout, BoothH, BoothL, multiplexer_3_out;

  Multiplexer #(.width(4), .enable("false")) multiplexer_1 (
    .in0(counter_1_q), .in1(DataOut[3:0]), .out(multiplexer_1_out), .sel(d2));
  Counter #(.width(4), .max('hf)) counter_1 (
    .load(controlunit_1_c2), .D(DataOut[3:0]), .count(controlunit_1_c1), .Q(counter_1_q), .clk(Clk),
    .clr(Reset));  // open: carry
  Register #(.width(4)) MAR (.D(multiplexer_1_out), .en(LoadMAR), .Q(Addr), .clk(Clk), .clr(Reset));
  Register #(.width(5)) IR (.D(DataOut[27:23]), .en(controlunit_1_c1), .clk(Clk), .clr(Reset));  // open: Q
  ControlUnit controlunit_1 (
    .IR(DataOut[27:23]), .Clk(Clk), .d1(d1), .c1(controlunit_1_c1), .R(R), .c2(controlunit_1_c2), .d2(d2),
    .b1(b1), .W(W), .LdAfrB(LdA_from_MBR), .Operation({c0, c1}), .LoadAc(LdA), .Reset(Reset),
    .bStart(bStart), .LdAfrL(LdAfrL), .LdAfrH(LdAfrH), .busy(booth_s_multiplier_1_busy));  // open: b2, b3
  Multiplexer #(.select(2), .width(28), .enable("false")) multiplexer_2 (
    .in0(ALUout), .in1(DataOut), .in2(BoothL), .in3(BoothH), .out(AcIn), .sel(or_1_out));
  or or_1 (or_1_out[0], LdA_from_MBR, LdAfrH);
  or or_2 (or_1_out[1], LdAfrL, LdAfrH);
  Multiplexer #(.width(28), .enable("false")) multiplexer_3 (.in0(dataIN), .in1(Ac), .out(multiplexer_3_out), .sel(b1));
  or or_3 (LoadMAR, d1, d2);
  Register #(.width(28)) MBR (.D(multiplexer_3_out), .en(LoadB), .Q(DataOut), .clk(Clk), .clr(Reset));
  Register #(.width(28)) u_Ac (.D(AcIn), .en(LoadAc), .Q(Ac), .clk(Clk), .clr(Reset));
  _28_bit_ALU_main main_1 (
    .A(Ac), .B(DataOut), .Control0(c0), .Control1(c1), .Result(ALUout));  // open: Zero, Negative, Overflow, Carry
  or or_4 (LoadB, R, b1);
  or or_5 (LoadAc, LdAfrL, LdA_from_MBR, LdA, LdAfrH);
  Booth_s_multiplier booth_s_multiplier_1 (
    .MBRout(DataOut), .Ac(Ac), .bStart(bStart), .in_4(Clk), .BoothsH(BoothH), .BoothsL(BoothL),
    .busy(booth_s_multiplier_1_busy));

  // Other names for the same wires on the sheet: clr = Reset; MBRout[27:0] = DataOut
endmodule

// CU
module ControlUnit (
  input  [4:0] IR,
  input  Clk,
  input  Reset,
  input  busy,
  output d1,
  output c1,
  output R,
  output c2,
  output d2,
  output [1:0] Operation,
  output b1,
  output W,
  output b2,
  output LoadAc,
  output b3,
  output LdAfrB,
  output bStart,
  output LdAfrL,
  output LdAfrH
);

  wire and_1_out, bWait, decoder_1_out6, decoder_1_out7, decoder_1_out8, decoder_1_out9, decoder_1_out15,
       nand_1_out, not_1_out, not_2_out, or_1_out, page;
  wire [5:0] counter_1_q;
  wire [6:0] rom_1_data;

  Counter #(.width(6), .max('h3f)) counter_1 (
    .load(rom_1_data[2]), .D({IR[3:0], 2'b11}), .count(rom_1_data[0]), .Q(counter_1_q), .clk(and_1_out),
    .clr(or_1_out));  // open: carry
  or or_1 (or_1_out, rom_1_data[1], Reset);
  and and_1 (and_1_out, Clk, nand_1_out, not_1_out);
  nand nand_1 (nand_1_out, busy, bWait);
  ROM #(.addrWidth(6)) rom_1 (.addr(counter_1_q), .data({page, rom_1_data}));  // open: sel
  not not_1 (not_1_out, decoder_1_out15);
  Decoder #(.select(4), .disabled(0)) decoder_1 (
    .out1(d1), .out2(c1), .out3(R), .out4(c2), .out5(d2), .out6(decoder_1_out6), .out7(decoder_1_out7),
    .out8(decoder_1_out8), .out9(decoder_1_out9), .out10(b1), .out11(W), .out12(b2), .out13(b3),
    .out14(LdAfrB), .out15(decoder_1_out15), .sel(rom_1_data[6:3]), .en(not_2_out));  // open: out0
  not not_2 (not_2_out, page);
  Priority_Encoder #(.select(2)) priority_encoder_1 (
    .in0(decoder_1_out6), .in1(decoder_1_out7), .in2(decoder_1_out8), .in3(decoder_1_out9), .out(Operation));  // open: gs, en_out, en_in
  // Pull_Resistor pull_resistor_1: pin names not known
  or or_2 (LoadAc, decoder_1_out6, decoder_1_out7, decoder_1_out8, decoder_1_out9);
  Decoder #(.select(2), .disabled(0)) decoder_2 (
    .out0(bStart), .out1(bWait), .out2(LdAfrL), .out3(LdAfrH), .sel(rom_1_data[4:3]), .en(page));

  // Notes on the sheet:
  //   contents of rom_1 (hex, n*v repeats v):
  //   9 19 14 29 19 31 2 29 19 39 2 29 51 59 2 29 19 41 2 29 19 49 2 21 2 2 2 29 19 71 2 78 2 2 2 61 39 2
  //   2 61 49 2 2 29 19 69 2 29 19 81 1 1 89 91 2 29 19 81 1 1 89 99 2 2
endmodule
