// Logisim project 28-bit-ALU.circ as structural Verilog: 9 circuits, main circuit main
module main (
  input  Control0,
  input  Control1,
  input  [27:0] A,
  input  [27:0] B,
  output [27:0] Result,
  output Zero,
  output Negative,
  output Overflow,
  output Carry
);

  wire undriven;
  wire [27:0] add_sub_1_result, multiplexer_1_out, n28_bit_and_1_result, n28_bit_or_1_result;

  _28_bit_and u_28_bit_and_1 (.A(A), .B(B), .Result(n28_bit_and_1_result));
  _28_bit_OR u_28_bit_or_1 (.A(A), .B(B), .Result(n28_bit_or_1_result));
  Add_sub add_sub_1 (.Sub(Control0), .A(A), .B(B), .Result(add_sub_1_result), .Carry(Carry), .Overflow(Overflow));
  Multiplexer #(.width(28), .enable("false")) multiplexer_1 (
    .in0(n28_bit_and_1_result), .in1(n28_bit_or_1_result), .out(multiplexer_1_out), .sel(Control0));
  Multiplexer #(.width(28), .enable("false")) multiplexer_2 (
    .in0(multiplexer_1_out), .in1(add_sub_1_result), .out(Result), .sel(Control1));
  _27th_bit_out u_27th_bit_out_1 (.Input(Result));  // open: out
  _28_bit_reduce_or u_28_bit_reduce_or_1 ();  // open: A, CONSTANT_ZERO, out_3
  not not_1 (Zero, undriven);
endmodule

// 28-bit AND
module _28_bit_and (
  input  [27:0] A,
  input  [27:0] B,
  output [27:0] Result
);

  assign Result = A & B;  // AND_Gate and_1, 28 bits wide
endmodule

// 28-bit OR
module _28_bit_OR (
  input  [27:0] A,
  input  [27:0] B,
  output [27:0] Result
);

  assign Result = A | B;  // OR_Gate or_1, 28 bits wide
endmodule

module Full_adder (
  input  Carry_in,
  input  A,
  input  B,
  output Result,
  output Carry_out
);

  wire and_1_out, and_2_out, xor_1_out;

  and and_1 (and_1_out, B, A);
  xor xor_1 (xor_1_out, A, B);
  or or_1 (Carry_out, and_1_out, and_2_out);
  and and_2 (and_2_out, xor_1_out, Carry_in);
  xor xor_2 (Result, Carry_in, xor_1_out);
endmodule

module _28_bit_full_adder (
  input  carry_in,
  input  [27:0] A,
  input  [27:0] B,
  output [27:0] RESULT_ADDER,
  output carry_out
);

  Adder #(.width(28)) adder_1 (.a(A), .b(B), .out(RESULT_ADDER), .cin(carry_in), .cout(carry_out));
endmodule

module _28_bit_xor (
  input  Control,
  input  [27:0] B,
  output [27:0] Result
);

  wire [27:0] bit_extender_1_out;

  assign bit_extender_1_out = {{27{Control}}, Control};  // Bit_Extender bit_extender_1
  assign Result = bit_extender_1_out ^ B;  // XOR_Gate xor_1, 28 bits wide
endmodule

// 8-bit \nADD/SUB
module Add_sub (
  input  Sub,
  input  [27:0] A,
  input  [27:0] B,
  output [27:0] Result,
  output Carry,
  output Overflow
);

  wire and_1_out, and_2_out, n27th_bit_out_1_out, n27th_bit_out_2_out, n27th_bit_out_3_out, not_1_out,
       not_2_out, not_3_out;
  wire [27:0] n28_bit_xor_1_result;

  _27th_bit_out u_27th_bit_out_1 (.Input(A), .out(n27th_bit_out_1_out));
  not not_1 (not_1_out, n27th_bit_out_1_out);
  _28_bit_xor u_28_bit_xor_1 (.B(B), .Result(n28_bit_xor_1_result), .Control(Sub));
  _27th_bit_out u_27th_bit_out_2 (.Input(B), .out(n27th_bit_out_2_out));
  not not_2 (not_2_out, n27th_bit_out_2_out);
  _28_bit_full_adder u_28_bit_full_adder_1 (
    .A(A), .B(n28_bit_xor_1_result), .RESULT_ADDER(Result), .carry_in(Sub), .carry_out(Carry));
  _27th_bit_out u_27th_bit_out_3 (.Input(Result), .out(n27th_bit_out_3_out));
  not not_3 (not_3_out, n27th_bit_out_3_out);
  and and_1 (and_1_out, not_3_out, n27th_bit_out_2_out, n27th_bit_out_1_out);
  and and_2 (and_2_out, n27th_bit_out_3_out, not_2_out, not_1_out);
  or or_1 (Overflow, and_1_out, and_2_out);

  // Notes on the sheet:
  //   A31
  //   B31
  //   Result 31
endmodule

// 27th
module _27th_bit_out (
  input  [27:0] Input,
  output out
);


  assign out = Input[27];
endmodule

// Reduce-OR
module _28_bit_reduce_or (
  input  [27:0] A,
  input  [27:0] CONSTANT_ZERO,
  output out_3
);

  Comparator #(.width(28), .mode("unsigned")) comparator_1 (.a(A), .b(CONSTANT_ZERO), .gt(out_3));  // open: eq, lt
endmodule
