// Logisim project thowa_fixed.circ as structural Verilog: 1 circuit, main circuit cache_28bit
module cache_28bit (
  input  clk,
  input  reset,
  input  rd,
  input  [3:0] addr,
  input  wr,
  input  [27:0] Wdata,
  output [27:0] Rdata,
  output hit,
  output miss
);

  wire and_1_out, and_2_out, and_3_out, and_4_out, and_5_out, and_6_out, and_7_out, and_8_out, and_9_out,
       and_10_out, and_11_out, and_12_out, comparator_1_eq, multiplexer_11_out, multiplexer_14_out,
       multiplexer_17_out, not_1_out, not_2_out, not_3_out, not_4_out, not_5_out, or_1_out, or_2_out,
       or_3_out, or_4_out, or_5_out, register_3_q, register_6_q, register_9_q, register_12_q;
  wire [1:0] multiplexer_2_out, multiplexer_4_out, multiplexer_6_out, multiplexer_8_out, multiplexer_10_out,
       multiplexer_13_out, multiplexer_16_out, register_2_q, register_5_q, register_8_q, register_11_q;
  wire [27:0] multiplexer_1_out, multiplexer_3_out, multiplexer_5_out, multiplexer_7_out, multiplexer_9_out,
       multiplexer_12_out, multiplexer_15_out, ram_1_data, register_1_q, register_4_q, register_7_q,
       register_10_q;

  not not_1 (not_1_out, reset);
  not not_2 (not_2_out, wr);
  RAM #(.addrWidth(4), .dataWidth(28)) ram_1 (
    .addr(addr), .data(ram_1_data), .sel(1'b1), .clk(clk), .ld(not_2_out), .clr(1'b0));
  assign ram_1_data = wr ? Wdata : 28'bz;  // Controlled_Buffer controlled_buffer_1
  not not_3 (not_3_out, addr[0]);
  not not_4 (not_4_out, addr[1]);
  and and_1 (and_1_out, not_4_out, not_3_out);
  and and_2 (and_2_out, not_4_out, addr[0]);
  and and_3 (and_3_out, addr[1], not_3_out);
  and and_4 (and_4_out, addr[1], addr[0]);
  and and_5 (and_5_out, and_1_out, or_5_out);
  and and_6 (and_6_out, and_2_out, or_5_out);
  and and_7 (and_7_out, and_3_out, or_5_out);
  and and_8 (and_8_out, and_4_out, or_5_out);
  Multiplexer #(.width(28)) multiplexer_1 (
    .in0(register_1_q), .in1(ram_1_data), .out(multiplexer_1_out), .sel(and_5_out));  // open: en
  Multiplexer #(.width(2)) multiplexer_2 (
    .in0(register_2_q), .in1(addr[3:2]), .out(multiplexer_2_out), .sel(and_5_out));  // open: en
  or or_1 (or_1_out, and_5_out, register_3_q);
  Multiplexer #(.width(28)) multiplexer_3 (
    .in0(register_4_q), .in1(ram_1_data), .out(multiplexer_3_out), .sel(and_6_out));  // open: en
  Multiplexer #(.width(2)) multiplexer_4 (
    .in0(register_5_q), .in1(addr[3:2]), .out(multiplexer_4_out), .sel(and_6_out));  // open: en
  or or_2 (or_2_out, and_6_out, register_6_q);
  Multiplexer #(.width(28)) multiplexer_5 (
    .in0(register_7_q), .in1(ram_1_data), .out(multiplexer_5_out), .sel(and_7_out));  // open: en
  Multiplexer #(.width(2)) multiplexer_6 (
    .in0(register_8_q), .in1(addr[3:2]), .out(multiplexer_6_out), .sel(and_7_out));  // open: en
  or or_3 (or_3_out, and_7_out, register_9_q);
  Multiplexer #(.width(28)) multiplexer_7 (
    .in0(register_10_q), .in1(ram_1_data), .out(multiplexer_7_out), .sel(and_8_out));  // open: en
  Multiplexer #(.width(2)) multiplexer_8 (
    .in0(register_11_q), .in1(addr[3:2]), .out(multiplexer_8_out), .sel(and_8_out));  // open: en
  or or_4 (or_4_out, and_8_out, register_12_q);
  Register #(.width(28)) register_1 (.D(multiplexer_1_out), .Q(register_1_q), .clk(clk));  // open: en, clr
  Register #(.width(2)) register_2 (.D(multiplexer_2_out), .Q(register_2_q), .clk(clk));  // open: en, clr
  Register #(.width(1)) register_3 (.D(and_9_out), .Q(register_3_q), .clk(clk));  // open: en, clr
  and and_9 (and_9_out, or_1_out, not_1_out);
  Register #(.width(28)) register_4 (.D(multiplexer_3_out), .Q(register_4_q), .clk(clk));  // open: en, clr
  Register #(.width(2)) register_5 (.D(multiplexer_4_out), .Q(register_5_q), .clk(clk));  // open: en, clr
  and and_10 (and_10_out, or_2_out, not_1_out);
  Register #(.width(1)) register_6 (.D(and_10_out), .Q(register_6_q), .clk(clk));  // open: en, clr
  Register #(.width(28)) register_7 (.D(multiplexer_5_out), .Q(register_7_q), .clk(clk));  // open: en, clr
  Register #(.width(2)) register_8 (.D(multiplexer_6_out), .Q(register_8_q), .clk(clk));  // open: en, clr
  Register #(.width(1)) register_9 (.D(and_11_out), .Q(register_9_q), .clk(clk));  // open: en, clr
  and and_11 (and_11_out, or_3_out, not_1_out);
  Register #(.width(28)) register_10 (.D(multiplexer_7_out), .Q(register_10_q), .clk(clk));  // open: en, clr
  Register #(.width(2)) register_11 (.D(multiplexer_8_out), .Q(register_11_q), .clk(clk));  // open: en, clr
  Register #(.width(1)) register_12 (.D(and_12_out), .Q(register_12_q), .clk(clk));  // open: en, clr
  and and_12 (and_12_out, or_4_out, not_1_out);
  Multiplexer #(.width(28)) multiplexer_9 (
    .in0(register_1_q), .in1(register_4_q), .out(multiplexer_9_out), .sel(addr[0]));  // open: en
  Multiplexer #(.width(2)) multiplexer_10 (
    .in0(register_2_q), .in1(register_5_q), .out(multiplexer_10_out), .sel(addr[0]));  // open: en
  Multiplexer multiplexer_11 (
    .in0(register_3_q), .in1(register_6_q), .out(multiplexer_11_out), .sel(addr[0]));  // open: en
  Multiplexer #(.width(28)) multiplexer_12 (
    .in0(register_7_q), .in1(register_10_q), .out(multiplexer_12_out), .sel(addr[0]));  // open: en
  Multiplexer #(.width(2)) multiplexer_13 (
    .in0(register_8_q), .in1(register_11_q), .out(multiplexer_13_out), .sel(addr[0]));  // open: en
  Multiplexer multiplexer_14 (
    .in0(register_9_q), .in1(register_12_q), .out(multiplexer_14_out), .sel(addr[0]));  // open: en
  Multiplexer #(.width(28)) multiplexer_15 (
    .in0(multiplexer_9_out), .in1(multiplexer_12_out), .out(multiplexer_15_out), .sel(addr[1]));  // open: en
  Multiplexer #(.width(2)) multiplexer_16 (
    .in0(multiplexer_10_out), .in1(multiplexer_13_out), .out(multiplexer_16_out), .sel(addr[1]));  // open: en
  Multiplexer multiplexer_17 (
    .in0(multiplexer_11_out), .in1(multiplexer_14_out), .out(multiplexer_17_out), .sel(addr[1]));  // open: en
  Comparator #(.width(2)) comparator_1 (.a(multiplexer_16_out), .b(addr[3:2]), .eq(comparator_1_eq));  // open: gt, lt
  and and_13 (hit, multiplexer_17_out, comparator_1_eq);
  not not_5 (not_5_out, hit);
  Multiplexer #(.width(28)) multiplexer_18 (
    .in0(ram_1_data), .in1(multiplexer_15_out), .out(Rdata), .sel(hit));  // open: en
  and and_14 (miss, not_5_out, rd);
  or or_5 (or_5_out, miss, wr);

  // Notes on the sheet:
  //   Cache controller inputs (clk, reset, rd, wr, addr, wdata)
  //   MAIN MEMORY (RAM 16 x 28)
  //   index = addr[1:0] (selects line), tag = addr[3:2]; MAR=addr 4 bit
  //   CACHE LINES 0..3  (data 28 | tag 2 | valid 1)
  //   READ MUX TREE (index selects line)
  //   HIT / MISS LOGIC
endmodule
